// Logisim project CPU_simulation_starter_2024.circ as structural Verilog: 3 circuits, main circuit CPU_main
module CPU_main (
);

  wire clock_1_out, instruction_decoding_unit_1_use_memory, instruction_decoding_unit_1_write_acc,
       instruction_decoding_unit_1_write_memory;
  wire [3:0] instruction_decoding_unit_1_alu_operation;
  wire [7:0] ACC_q, adder_1_out, alu_1_alu_to_acc, instruction_decoding_unit_1_addr_or_imm, Memory_B_dout,
       multiplexer_1_out, PC_q;
  wire [15:0] Memory_A_data;

  Clock clock_1 (.out(clock_1_out));
  Adder adder_1 (.a(PC_q), .b(8'h1), .out(adder_1_out));  // open: cin, cout
  Register PC (.D(adder_1_out), .clk(clock_1_out), .Q(PC_q));  // open: en, clr
  ROM #(.dataWidth(16)) Memory_A (.addr(PC_q), .data(Memory_A_data));
  Instruction_Decoding_Unit instruction_decoding_unit_1 (
    .Instruction(Memory_A_data), .ALU_Operation(instruction_decoding_unit_1_alu_operation),
    .Write_ACC(instruction_decoding_unit_1_write_acc), .Use_Memory(instruction_decoding_unit_1_use_memory),
    .Write_Memory(instruction_decoding_unit_1_write_memory),
    .Addr_or_Imm(instruction_decoding_unit_1_addr_or_imm));  // open: BNEZ, Output_Char, Stop
  RAM #(.asyncread("true"), .clearpin("true")) Memory_B (
    .addr(instruction_decoding_unit_1_addr_or_imm), .we(instruction_decoding_unit_1_write_memory),
    .clk(clock_1_out), .din(ACC_q), .dout(Memory_B_dout));  // open: oe, clr
  Register ACC (
    .D(alu_1_alu_to_acc), .en(instruction_decoding_unit_1_write_acc), .clk(clock_1_out), .Q(ACC_q));  // open: clr
  Multiplexer #(.width(8)) multiplexer_1 (
    .in0(instruction_decoding_unit_1_addr_or_imm), .in1(Memory_B_dout), .out(multiplexer_1_out),
    .sel(instruction_decoding_unit_1_use_memory));
  ALU alu_1 (
    .ALU_Operation(instruction_decoding_unit_1_alu_operation), .From_ACC(ACC_q), .Input2(multiplexer_1_out),
    .ALU_to_ACC(alu_1_alu_to_acc));  // open: ACC_NE_Zero

  // Notes on the sheet:
  //   Student id: 00000000
endmodule

module Instruction_Decoding_Unit (
  input  [15:0] Instruction,
  output [3:0] ALU_Operation,
  output Write_ACC,
  output Use_Memory,
  output Write_Memory,
  output BNEZ,
  output Output_Char,
  output Stop,
  output [7:0] Addr_or_Imm
);

  wire decoder_1_out1, decoder_1_out2;

  Decoder #(.select(4)) decoder_1 (
    .out1(decoder_1_out1), .out2(decoder_1_out2), .out3(Write_Memory), .out4(BNEZ), .out5(Output_Char),
    .out15(Stop), .sel(Instruction[15:12]));  // open: out0, out6, out7, out8, out9, out10, out11, out12, out13, out14, en
  or or_1 (Write_ACC, decoder_1_out1, decoder_1_out2);
  or or_2 (Use_Memory, decoder_1_out2, Write_Memory);

  assign Addr_or_Imm = Instruction[7:0];
  assign ALU_Operation = Instruction[11:8];
endmodule

module ALU (
  input  [3:0] ALU_Operation,
  input  [7:0] From_ACC,
  input  [7:0] Input2,
  output [7:0] ALU_to_ACC,
  output ACC_NE_Zero
);

  wire [7:0] adder_1_out, and_1_out, xor_1_out;

  Adder adder_1 (.a(From_ACC), .b(Input2), .out(adder_1_out));  // open: cin, cout
  assign and_1_out = From_ACC & Input2;  // AND_Gate and_1, 8 bits wide
  assign xor_1_out = From_ACC ^ Input2;  // XOR_Gate xor_1, 8 bits wide
  Multiplexer #(.select(4), .width(8)) multiplexer_1 (
    .in0(Input2), .in1(adder_1_out), .in2(and_1_out), .in3(xor_1_out), .out(ALU_to_ACC), .sel(ALU_Operation));  // open: in4, in5, in6, in7, in8, in9, in10, in11, in12, in13, in14, in15
endmodule
